# Fritzing sketch lcd_spotify (saved by Fritzing 0.9.3b)

parts:
  MCU1 = Raspberry Pi Zero
  S1 = Square Pushbutton
  Part2 = LCD1602-I2C

nets:
  N1: MCU1.pin_1, Part2.VCC
  N2: MCU1.pin_3, Part2.SDA
  N3: MCU1.pin_5, Part2.SCL
  N4: MCU1.pin_9, MCU1.pin_39, S1.leg0, Part2.GND
  N5: MCU1.pin_37, S1.leg1

custom parts:
  LCD1602-I2C: A standard character display, usually with 2x16 characters. Comes in many colors with LCM1602 IIC attached.
